// Logisim project second_task.circ as structural Verilog: 1 circuit, main circuit main
module main (
  input  x4,
  input  x3,
  input  x2,
  input  x1,
  output y1,
  output y2,
  output y3,
  output y4
);

  wire not_1_out, not_2_out, not_3_out, not_4_out, or_1_out, or_2_out, or_3_out, or_4_out, or_5_out,
       or_6_out, or_7_out, or_8_out, or_9_out, or_10_out;

  not not_1 (not_1_out, x4);
  not not_2 (not_2_out, x3);
  not not_3 (not_3_out, x2);
  not not_4 (not_4_out, x1);
  or or_1 (or_1_out, not_4_out, x2, x3);
  or or_2 (or_2_out, x4, not_4_out);
  or or_3 (or_3_out, x1, x2, x4);
  or or_4 (or_4_out, not_4_out, not_3_out, x4);
  or or_5 (or_5_out, x1, x2, x3, not_1_out);
  or or_6 (or_6_out, x1, x3, x4);
  or or_7 (or_7_out, x2, x3);
  or or_8 (or_8_out, not_4_out, not_3_out, not_2_out, x4);
  or or_9 (or_9_out, not_4_out, not_3_out, not_2_out, x4);
  or or_10 (or_10_out, x2, x3, not_1_out);
  and and_1 (y1, or_1_out, or_2_out);
  and and_2 (y2, or_3_out, or_4_out, or_5_out);
  and and_3 (y3, or_6_out, or_7_out, or_8_out);
  and and_4 (y4, or_9_out, or_10_out);
endmodule
